# Fritzing sketch OMA_v1 (saved by Fritzing 0.9.3b)
circuit board: 8.46667cm x 5.64444cm
circuit board: 5.33408cm x 3.52994cm

parts:
  U1 = ESP8266 WiFi Module [part_number=ESP8266]
  LED-Streifen = ws2812b [package="smd 2812b"]
  U2 = V_REG_LD1117VXX [package=78xxl]
  Power_plug1 = Power plug
  JP1 = Header 4 [package=screwterminal-3.5mm-4_lock]
  R1 = Resistor [tolerance=±5% resistance=10k package="1206 [SMD]"]
  R2 = Resistor [tolerance=±5% resistance=10k package="1206 [SMD]"]
  JP2 = Header 4 [package=screwterminal-3.5mm-4_lock]
  Grove1 = Grove OLED 128x96
  MCP1 = MCP23008 - 8-bit GPIO expander I2C [package="DIP (Dual Inline) [THT]"]

nets:
  N1: U1.GPIO_2, LED-Streifen.DIN
  N2: U1.CH_PD, R1.Pin_1
  GND: U1.GND, LED-Streifen.VSS, U2.GND, Power_plug1.GND, JP1.4, R2.Pin_1
  N3: U1.GPIO_15, R2.Pin_0
  N4: U1.GPIO_4, JP1.2
  N5: U1.GPIO_5, JP1.3
  VDD: LED-Streifen.VDD, U2.IN, Power_plug1.VCC
  N6: U2.OUT, JP1.1, R1.Pin_0
  VCC: JP2.1, Grove1.VCC, MCP1.VDD
  GND_2: JP2.2, Grove1.GND, MCP1.VSS
  N7: JP2.3, Grove1.SCL, MCP1.SCL
  N8: JP2.4, Grove1.SDA, MCP1.SDA

custom parts:
  MCP23008 - 8-bit GPIO expander I2C: The MCP23008 device provides 8-bit, general purpose, parallel I/O expansion for I2C bus.
